// Logisim project fibnacci_32bit.circ as structural Verilog: 4 circuits, main circuit main
module main (
  input  [31:0] in_1
);

  wire clk, not_1_out, reset, sig, stop;
  wire [31:0] matmult_1_out_9, matmult_1_out_10, matmult_1_out_11, matmult_1_out_12, undriven, undriven_2,
       undriven_3, undriven_4, undriven_5, undriven_6, undriven_7, undriven_8;

  Clock clock_1 (.out(clk));
  not not_1 (not_1_out, reset);
  Register #(.width(1)) register_1 (.D(stop), .en(not_1_out), .Q(reset), .clk(clk));  // open: clr
  poiter poiter_1 (.in_1(in_1), .in_2(reset), .out_3(sig), .out_4(stop));
  matMult matmult_1 (
    .in_1(undriven), .in_2(undriven_2), .in_3(undriven_3), .in_4(undriven_4), .in_5(undriven_5),
    .in_6(undriven_6), .in_7(undriven_7), .in_8(undriven_8), .out_9(matmult_1_out_9),
    .out_10(matmult_1_out_10), .out_11(matmult_1_out_11), .out_12(matmult_1_out_12));
endmodule

module matMult (
  input  [31:0] in_1,
  input  [31:0] in_2,
  input  [31:0] in_3,
  input  [31:0] in_4,
  input  [31:0] in_5,
  input  [31:0] in_6,
  input  [31:0] in_7,
  input  [31:0] in_8,
  output [31:0] out_9,
  output [31:0] out_10,
  output [31:0] out_11,
  output [31:0] out_12
);

  wire [31:0] multiplier_1_out, multiplier_2_out, multiplier_3_out, multiplier_4_out, multiplier_5_out,
       multiplier_6_out, multiplier_7_out, multiplier_8_out;

  Multiplier #(.width(32)) multiplier_1 (.a(in_1), .b(in_2), .out(multiplier_1_out));  // open: cin, cout
  Multiplier #(.width(32)) multiplier_2 (.a(in_3), .b(in_6), .out(multiplier_2_out));  // open: cin, cout
  Multiplier #(.width(32)) multiplier_3 (.a(in_4), .b(in_5), .out(multiplier_3_out));  // open: cin, cout
  Multiplier #(.width(32)) multiplier_4 (.a(in_7), .b(in_8), .out(multiplier_4_out));  // open: cin, cout
  Multiplier #(.width(32)) multiplier_5 (.a(in_1), .b(in_4), .out(multiplier_5_out));  // open: cin, cout
  Multiplier #(.width(32)) multiplier_6 (.a(in_3), .b(in_8), .out(multiplier_6_out));  // open: cin, cout
  Multiplier #(.width(32)) multiplier_7 (.a(in_2), .b(in_5), .out(multiplier_7_out));  // open: cin, cout
  Multiplier #(.width(32)) multiplier_8 (.a(in_6), .b(in_7), .out(multiplier_8_out));  // open: cin, cout
  Adder #(.width(32)) adder_1 (.a(multiplier_1_out), .b(multiplier_2_out), .out(out_9));  // open: cin, cout
  Adder #(.width(32)) adder_2 (.a(multiplier_3_out), .b(multiplier_4_out), .out(out_12));  // open: cin, cout
  Adder #(.width(32)) adder_3 (.a(multiplier_5_out), .b(multiplier_6_out), .out(out_10));  // open: cin, cout
  Adder #(.width(32)) adder_4 (.a(multiplier_7_out), .b(multiplier_8_out), .out(out_11));  // open: cin, cout

  // Other names for the same wires on the sheet: matA_1_1[31:0] = in_1; matA_1_2[31:0] = in_3; matA_2_1[31:0] = in_5;
  //   matA_2_2[31:0] = in_7; matB_1_1[31:0] = in_2; matB_1_2[31:0] = in_4; matB_2_1[31:0] = in_6;
  //   matB_2_2[31:0] = in_8; matC_1_1[31:0] = out_9; matC_1_2[31:0] = out_10; matC_2_1[31:0] = out_11;
  //   matC_2_2[31:0] = out_12
endmodule

module poiter (
  input  [31:0] in_1,
  input  in_2,
  output out_3,
  output out_4
);

  wire clk;
  wire [4:0] counter_1_q;

  Clock clock_1 (.out(clk));
  Counter #(.width(5), .max('h1f), .ongoal("stay")) counter_1 (
    .Q(counter_1_q), .clk(clk), .clr(in_2));  // open: load, D, count, carry
  BitSelector #(.width(32)) bitselector_1 (.in(in_1), .out(out_3), .sel(counter_1_q));
  Comparator #(.width(5)) comparator_1 (.a(counter_1_q), .b({5{1'b1}}), .eq(out_4));  // open: gt, lt

  // Other names for the same wires on the sheet: reset = in_2
endmodule

module matReg (
  input  [31:0] in_1,
  input  [31:0] in_2,
  input  [31:0] in_3,
  input  [31:0] in_4,
  input  in_5,
  output [31:0] out_6,
  output [31:0] out_7,
  output [31:0] out_8,
  output [31:0] out_9
);

  wire clk;

  Clock clock_1 (.out(clk));
  Register #(.width(32)) register_1 (.D(in_1), .en(in_5), .Q(out_6), .clk(clk));  // open: clr
  Register #(.width(32)) register_2 (.D(in_2), .en(in_5), .Q(out_7), .clk(clk));  // open: clr
  Register #(.width(32)) register_3 (.D(in_3), .en(in_5), .Q(out_8), .clk(clk));  // open: clr
  Register #(.width(32)) register_4 (.D(in_4), .en(in_5), .Q(out_9), .clk(clk));  // open: clr

  // Other names for the same wires on the sheet: enable = in_5
endmodule
